# Fritzing sketch raspberrypi-atx (saved by Fritzing 0.9.3b)
circuit board: 3.9cm x 2.7cm
breadboards: 2

parts:
  U1 = ATTINY45 [part_number=ATtiny45 package=dip]
  J1 = ATX24 Pin Power Supply Connector [package=atx24_right_angle]
  S1 = Round Pushbutton [part_number=Pushbutton]
  R1 = Resistor [tolerance=±5% resistance=1k package=THT]
  R2 = Resistor [tolerance=±5% resistance=220 package=THT]
  LED1 = LED - 5mm [color="Red (633nm)" package="5 mm [THT]"]
  R3 = Resistor [tolerance=±5% resistance=47k package=THT]
  R4 = Resistor [tolerance=±5% resistance=100k package=THT]
  Q1 = MOSFET-NCHANNEL [part_number="IRLML 25002TR" package=sot23-3]
  C2 = Ceramic Capacitor [capacitance=100nF package="100 mil [THT, multilayer]"]
  C1 = Ceramic Capacitor [capacitance=100nF package="200 mil [THT, multilayer]"]
  Q2 = Basic FET P-Channel [part_number=IRF4905 package="TO220 [THT]"]
  R5 = Resistor [tolerance=±5% resistance=10k package=THT]
  R6 = Resistor [tolerance=±5% resistance=100 package=THT]
  R7 = Resistor [tolerance=±5% resistance=4.7k package=THT]
  R8 = Resistor [tolerance=±5% resistance=100 package=THT]
  Q3 = NPN-Transistor [part_number=BC548C package="TO92 [THT]"]
  R9 = Resistor [tolerance=±5% resistance=100k package=THT]
  R10 = Resistor [tolerance=±5% resistance=1k package=THT]

nets:
  NC: U1.PB5(NRES)
  N1: U1.PB3(ADC3), R3.Pin_1
  up from RaspberryPi: U1.PB4(ADC2)
  GND: U1.GND, J1.GND, S1.leg0, R2.Pin_1, R4.Pin_0, Q1.S, C2.1, C1.1, Q3.C, R9.Pin_1
  N2: U1.PB0(MOSI), R8.Pin_0
  N3: U1.PB1(MISO), R1.Pin_0, C2.0
  N4: U1.PB2(SCK_ADC1), LED1.anode
  N5: U1.VCC, J1.5V_STDBY, C1.0
  N6: J1.5V, Q2.source, R5.Pin_0
  N7: J1.PWR_OK, R7.Pin_0
  N8: J1.PS_ON, R10.Pin_1
  N9: S1.leg1, R1.Pin_1
  N10: R2.Pin_0, LED1.cathode
  shutdown to RaspberryPi: R3.Pin_0, R4.Pin_1
  N11: Q1.G, R8.Pin_1, R9.Pin_0
  N12: Q1.D, R10.Pin_0
  N13: Q2.gate, R5.Pin_1, R6.Pin_1
  VCC RaspberryPi: Q2.drain
  N14: R6.Pin_0, Q3.E
  N15: R7.Pin_1, Q3.B

notes:
  GND
  5V+
  <--BASE- LOAD->
  UP
  ON
  SHD
  +
  BTN
  LED
  STDB
  GOOD
  RasPelikan
  ~
  NC
